// Logisim project 16bit.circ as structural Verilog: 1 circuit, main circuit main
module main (
);

  wire adder_1_cout, clock_1_out, decoder_1_out0, decoder_1_out1, decoder_1_out2, decoder_1_out3,
       decoder_1_out4, decoder_1_out5, decoder_1_out6, decoder_1_out7, decoder_1_out8, decoder_2_out0,
       decoder_2_out1, decoder_2_out2, decoder_2_out3, decoder_2_out4, decoder_2_out5, decoder_2_out6,
       decoder_2_out7, decoder_2_out8, decoder_2_out9, decoder_2_out10, decoder_2_out11, decoder_2_out12,
       decoder_2_out13, decoder_2_out14, decoder_2_out15, not_1_out, not_2_out, PC_carry;
  wire [3:0] T_q;
  wire [15:0] adder_1_out, controlled_buffer_1_out, controlled_buffer_7_out, controlled_buffer_8_out,
       dipswitch_1_sw16, GPIO1_q, GPIO2_q, IR_q, PC_q, R1_q, R2_q, RAMA_q, register_1_q, register_2_q,
       register_3_q, register_4_q, register_5_q, register_6_q, register_7_q, register_8_q, register_9_q,
       register_10_q, register_11_q, register_12_q, register_13_q, register_14_q, register_15_q, rom_1_data,
       ROMA_q, ROW0_q, ROW15_q;
  wire [19:0] INS_data;

  Clock clock_1 (.out(clock_1_out));
  DipSwitch #(.number(16)) dipswitch_1 (
    .sw1(dipswitch_1_sw16[15]), .sw2(dipswitch_1_sw16[14]), .sw3(dipswitch_1_sw16[13]),
    .sw4(dipswitch_1_sw16[12]), .sw5(dipswitch_1_sw16[11]), .sw6(dipswitch_1_sw16[10]),
    .sw7(dipswitch_1_sw16[9]), .sw8(dipswitch_1_sw16[8]), .sw9(dipswitch_1_sw16[7]),
    .sw10(dipswitch_1_sw16[6]), .sw11(dipswitch_1_sw16[5]), .sw12(dipswitch_1_sw16[4]),
    .sw13(dipswitch_1_sw16[3]), .sw14(dipswitch_1_sw16[2]), .sw15(dipswitch_1_sw16[1]),
    .sw16(dipswitch_1_sw16[0]));
  LED led_1 (.in(INS_data[17]));
  LED led_2 (.in(INS_data[16]));
  LED led_3 (.in(INS_data[15]));
  LED led_4 (.in(INS_data[14]));
  LED led_5 (.in(INS_data[13]));
  LED led_6 (.in(INS_data[12]));
  assign controlled_buffer_1_out = 1'b0 ? dipswitch_1_sw16 : 16'bz;  // Controlled_Buffer controlled_buffer_1
  LED led_7 (.in(INS_data[11]));
  LED led_8 (.in(INS_data[10]));
  LED led_9 (.in(INS_data[9]));
  LED led_10 (.in(INS_data[8]));
  LED led_11 (.in(INS_data[7]));
  LED led_12 (.in(INS_data[6]));
  Register #(.width(16), .trigger("high")) R1 (
    .D(controlled_buffer_1_out), .en(INS_data[16]), .clk(clock_1_out), .Q(R1_q));  // open: clr
  LED led_13 (.in(INS_data[5]));
  LED led_14 (.in(controlled_buffer_1_out[15]));
  assign controlled_buffer_1_out = INS_data[15] ? R1_q : 16'bz;  // Controlled_Buffer controlled_buffer_2
  assign controlled_buffer_1_out = INS_data[13] ? R2_q : 16'bz;  // Controlled_Buffer controlled_buffer_3
  Register #(.width(16), .trigger("high")) R2 (
    .D(controlled_buffer_1_out), .en(INS_data[14]), .clk(clock_1_out), .Q(R2_q));  // open: clr
  Register #(.width(16), .trigger("high")) RAMA (
    .D(controlled_buffer_1_out), .en(INS_data[12]), .clk(clock_1_out), .Q(RAMA_q));  // open: clr
  Register #(.width(16), .trigger("high")) ROMA (
    .D(controlled_buffer_1_out), .en(INS_data[9]), .clk(clock_1_out), .Q(ROMA_q));  // open: clr
  LED led_15 (.in(controlled_buffer_1_out[11]));
  LED led_16 (.in(controlled_buffer_1_out[14]));
  LED led_17 (.in(controlled_buffer_1_out[12]));
  LED led_18 (.in(controlled_buffer_1_out[13]));
  LED led_19 (.in(R1_q[13]));
  LED led_20 (.in(R1_q[15]));
  LED led_21 (.in(R1_q[14]));
  LED led_22 (.in(R1_q[12]));
  LED led_23 (.in(R2_q[13]));
  LED led_24 (.in(R2_q[14]));
  LED led_25 (.in(R2_q[15]));
  LED led_26 (.in(RAMA_q[15]));
  LED led_27 (.in(RAMA_q[14]));
  LED led_28 (.in(RAMA_q[12]));
  LED led_29 (.in(RAMA_q[13]));
  LED led_30 (.in(ROMA_q[15]));
  LED led_31 (.in(ROMA_q[13]));
  LED led_32 (.in(ROMA_q[14]));
  LED led_33 (.in(INS_data[4]));
  LED led_34 (.in(INS_data[3]));
  LED led_35 (.in(INS_data[2]));
  LED led_36 (.in(controlled_buffer_1_out[8]));
  LED led_37 (.in(controlled_buffer_1_out[7]));
  LED led_38 (.in(controlled_buffer_1_out[10]));
  LED led_39 (.in(controlled_buffer_1_out[9]));
  LED led_40 (.in(R1_q[10]));
  LED led_41 (.in(R1_q[9]));
  LED led_42 (.in(R1_q[11]));
  LED led_43 (.in(R1_q[8]));
  LED led_44 (.in(R2_q[11]));
  LED led_45 (.in(R2_q[10]));
  LED led_46 (.in(R2_q[12]));
  LED led_47 (.in(R2_q[9]));
  LED led_48 (.in(RAMA_q[8]));
  LED led_49 (.in(RAMA_q[10]));
  LED led_50 (.in(RAMA_q[9]));
  LED led_51 (.in(RAMA_q[11]));
  LED led_52 (.in(ROMA_q[9]));
  LED led_53 (.in(ROMA_q[11]));
  LED led_54 (.in(ROMA_q[10]));
  LED led_55 (.in(ROMA_q[12]));
  LED led_56 (.in(INS_data[1]));
  LED led_57 (.in(controlled_buffer_1_out[4]));
  LED led_58 (.in(controlled_buffer_1_out[6]));
  LED led_59 (.in(controlled_buffer_1_out[3]));
  LED led_60 (.in(controlled_buffer_1_out[5]));
  LED led_61 (.in(R1_q[6]));
  LED led_62 (.in(R1_q[5]));
  LED led_63 (.in(R1_q[7]));
  LED led_64 (.in(R1_q[4]));
  LED led_65 (.in(R2_q[8]));
  LED led_66 (.in(R2_q[6]));
  LED led_67 (.in(R2_q[7]));
  LED led_68 (.in(R2_q[5]));
  LED led_69 (.in(RAMA_q[6]));
  LED led_70 (.in(RAMA_q[4]));
  LED led_71 (.in(RAMA_q[7]));
  LED led_72 (.in(RAMA_q[5]));
  LED led_73 (.in(ROMA_q[5]));
  LED led_74 (.in(ROMA_q[6]));
  LED led_75 (.in(ROMA_q[7]));
  LED led_76 (.in(ROMA_q[8]));
  LED led_77 (.in(INS_data[0]));
  LED led_78 (.in(controlled_buffer_1_out[0]));
  LED led_79 (.in(controlled_buffer_1_out[1]));
  LED led_80 (.in(controlled_buffer_1_out[2]));
  LED led_81 (.in(R1_q[2]));
  LED led_82 (.in(R1_q[1]));
  LED led_83 (.in(R1_q[3]));
  LED led_84 (.in(R1_q[0]));
  LED led_85 (.in(R2_q[2]));
  LED led_86 (.in(R2_q[3]));
  LED led_87 (.in(R2_q[4]));
  LED led_88 (.in(R2_q[1]));
  LED led_89 (.in(RAMA_q[2]));
  LED led_90 (.in(RAMA_q[3]));
  LED led_91 (.in(RAMA_q[1]));
  LED led_92 (.in(RAMA_q[0]));
  LED led_93 (.in(ROMA_q[4]));
  LED led_94 (.in(ROMA_q[3]));
  LED led_95 (.in(ROMA_q[2]));
  LED led_96 (.in(ROMA_q[1]));
  LED led_97 (.in(R2_q[0]));
  LED led_98 (.in(ROMA_q[0]));
  LED led_99 (.in(adder_1_cout));
  Register #(.width(16), .trigger("high")) register_1 (
    .D(adder_1_out), .en(INS_data[5]), .clk(clock_1_out), .Q(register_1_q));  // open: clr
  Adder #(.width(16)) adder_1 (.a(R1_q), .b(R2_q), .out(adder_1_out), .cout(adder_1_cout));  // open: cin
  RAM #(.addrWidth(16), .dataWidth(16)) ram_1 (
    .addr(RAMA_q), .we(INS_data[11]), .oe(INS_data[10]), .clk(clock_1_out), .data(controlled_buffer_1_out));
  ROM #(.addrWidth(16), .dataWidth(16)) rom_1 (.addr(ROMA_q), .data(rom_1_data));
  assign controlled_buffer_1_out = INS_data[17] ? register_1_q : 16'bz;  // Controlled_Buffer controlled_buffer_4
  assign controlled_buffer_1_out = INS_data[8] ? rom_1_data : 16'bz;  // Controlled_Buffer controlled_buffer_5
  not not_1 (not_1_out, clock_1_out);
  Register #(.width(16), .trigger("high")) GPIO1 (
    .D(controlled_buffer_1_out), .en(INS_data[7]), .clk(clock_1_out), .Q(GPIO1_q));  // open: clr
  Register #(.width(16), .trigger("high")) GPIO2 (
    .D(controlled_buffer_1_out), .en(INS_data[6]), .clk(clock_1_out), .Q(GPIO2_q));  // open: clr
  LED led_100 (.in(GPIO1_q[15]));
  LED led_101 (.in(GPIO2_q[15]));
  Counter #(.width(4), .max('hf)) T (
    .clr(decoder_1_out5), .load(1'b0), .up(1'b1), .clk(not_1_out), .Q(T_q));  // open: count, D, carry
  Decoder #(.select(4)) decoder_1 (
    .out0(decoder_1_out0), .out1(decoder_1_out1), .out2(decoder_1_out2), .out3(decoder_1_out3),
    .out4(decoder_1_out4), .out5(decoder_1_out5), .out6(decoder_1_out6), .out7(decoder_1_out7),
    .out8(decoder_1_out8), .sel(T_q));  // open: out9, out10, out11, out12, out13, out14, out15, en
  Register #(.width(16), .trigger("high")) IR (
    .D(controlled_buffer_1_out), .en(INS_data[1]), .clk(clock_1_out), .Q(IR_q));  // open: clr
  LED led_102 (.in(IR_q[15]));
  LED led_103 (.in(IR_q[14]));
  LED led_104 (.in(GPIO1_q[14]));
  LED led_105 (.in(GPIO1_q[13]));
  LED led_106 (.in(GPIO1_q[11]));
  LED led_107 (.in(GPIO1_q[12]));
  LED led_108 (.in(GPIO2_q[14]));
  LED led_109 (.in(GPIO2_q[13]));
  LED led_110 (.in(GPIO2_q[11]));
  LED led_111 (.in(GPIO2_q[12]));
  Counter #(.width(16), .max('hffff)) PC (
    .clr(1'b0), .load(INS_data[4]), .up(1'b1), .count(INS_data[2]), .clk(clock_1_out),
    .D(controlled_buffer_1_out), .carry(PC_carry), .Q(PC_q));
  LED led_112 (.in(IR_q[13]));
  LED led_113 (.in(IR_q[12]));
  LED led_114 (.in(IR_q[10]));
  LED led_115 (.in(IR_q[11]));
  ROM #(.addrWidth(16), .dataWidth(20)) INS (.addr({4'b0000, T_q, IR_q[15:8]}), .data(INS_data));
  LED led_116 (.in(GPIO1_q[8]));
  LED led_117 (.in(GPIO1_q[9]));
  LED led_118 (.in(GPIO1_q[7]));
  LED led_119 (.in(GPIO1_q[10]));
  LED led_120 (.in(GPIO2_q[7]));
  LED led_121 (.in(GPIO2_q[8]));
  LED led_122 (.in(GPIO2_q[9]));
  LED led_123 (.in(GPIO2_q[10]));
  assign controlled_buffer_1_out = INS_data[3] ? PC_q : 16'bz;  // Controlled_Buffer controlled_buffer_6
  LED led_124 (.in(decoder_1_out0));
  LED led_125 (.in(decoder_1_out1));
  LED led_126 (.in(decoder_1_out2));
  LED led_127 (.in(decoder_1_out3));
  LED led_128 (.in(decoder_1_out4));
  LED led_129 (.in(IR_q[7]));
  LED led_130 (.in(IR_q[6]));
  LED led_131 (.in(IR_q[8]));
  LED led_132 (.in(IR_q[9]));
  assign controlled_buffer_7_out = 1'b1 ? GPIO1_q : 16'bz;  // Controlled_Buffer controlled_buffer_7
  LED led_133 (.in(GPIO1_q[5]));
  LED led_134 (.in(GPIO1_q[6]));
  LED led_135 (.in(GPIO1_q[3]));
  LED led_136 (.in(GPIO1_q[4]));
  LED led_137 (.in(GPIO2_q[4]));
  LED led_138 (.in(GPIO2_q[5]));
  LED led_139 (.in(GPIO2_q[6]));
  LED led_140 (.in(GPIO2_q[3]));
  LED led_141 (.in(IR_q[2]));
  LED led_142 (.in(IR_q[5]));
  LED led_143 (.in(IR_q[4]));
  LED led_144 (.in(IR_q[3]));
  LED led_145 (.in(GPIO1_q[1]));
  LED led_146 (.in(GPIO1_q[2]));
  LED led_147 (.in(GPIO1_q[0]));
  assign controlled_buffer_8_out = 1'b1 ? GPIO2_q : 16'bz;  // Controlled_Buffer controlled_buffer_8
  LED led_148 (.in(GPIO2_q[2]));
  LED led_149 (.in(GPIO2_q[1]));
  LED led_150 (.in(GPIO2_q[0]));
  LED led_151 (.in(PC_carry));
  LED led_152 (.in(IR_q[1]));
  LED led_153 (.in(IR_q[0]));
  not not_2 (not_2_out, clock_1_out);
  Decoder #(.select(4)) decoder_2 (
    .out0(decoder_2_out0), .out1(decoder_2_out1), .out2(decoder_2_out2), .out3(decoder_2_out3),
    .out4(decoder_2_out4), .out5(decoder_2_out5), .out6(decoder_2_out6), .out7(decoder_2_out7),
    .out8(decoder_2_out8), .out9(decoder_2_out9), .out10(decoder_2_out10), .out11(decoder_2_out11),
    .out12(decoder_2_out12), .out13(decoder_2_out13), .out14(decoder_2_out14), .out15(decoder_2_out15),
    .sel(controlled_buffer_8_out[3:0]), .en(not_2_out));
  assign controlled_buffer_1_out = INS_data[0] ? {{8{1'b0}}, IR_q[7:0]} : 16'bz;  // Controlled_Buffer controlled_buffer_9
  Register #(.width(16), .trigger("high")) ROW0 (
    .D(controlled_buffer_7_out), .en(decoder_2_out0), .clk(clock_1_out), .Q(ROW0_q));  // open: clr
  Register #(.width(16), .trigger("high")) register_2 (
    .D(controlled_buffer_7_out), .en(decoder_2_out1), .clk(clock_1_out), .Q(register_2_q));  // open: clr
  Register #(.width(16), .trigger("high")) register_3 (
    .D(controlled_buffer_7_out), .en(decoder_2_out2), .clk(clock_1_out), .Q(register_3_q));  // open: clr
  Register #(.width(16), .trigger("high")) register_4 (
    .D(controlled_buffer_7_out), .en(decoder_2_out3), .clk(clock_1_out), .Q(register_4_q));  // open: clr
  Register #(.width(16), .trigger("high")) register_5 (
    .D(controlled_buffer_7_out), .en(decoder_2_out4), .clk(clock_1_out), .Q(register_5_q));  // open: clr
  Register #(.width(16), .trigger("high")) register_6 (
    .D(controlled_buffer_7_out), .en(decoder_2_out5), .clk(clock_1_out), .Q(register_6_q));  // open: clr
  Register #(.width(16), .trigger("high")) register_7 (
    .D(controlled_buffer_7_out), .en(decoder_2_out6), .clk(clock_1_out), .Q(register_7_q));  // open: clr
  Register #(.width(16), .trigger("high")) register_8 (
    .D(controlled_buffer_7_out), .en(decoder_2_out7), .clk(clock_1_out), .Q(register_8_q));  // open: clr
  Register #(.width(16), .trigger("high")) register_9 (
    .D(controlled_buffer_7_out), .en(decoder_2_out8), .clk(clock_1_out), .Q(register_9_q));  // open: clr
  Register #(.width(16), .trigger("high")) register_10 (
    .D(controlled_buffer_7_out), .en(decoder_2_out9), .clk(clock_1_out), .Q(register_10_q));  // open: clr
  Register #(.width(16), .trigger("high")) register_11 (
    .D(controlled_buffer_7_out), .en(decoder_2_out10), .clk(clock_1_out), .Q(register_11_q));  // open: clr
  Register #(.width(16), .trigger("high")) register_12 (
    .D(controlled_buffer_7_out), .en(decoder_2_out11), .clk(clock_1_out), .Q(register_12_q));  // open: clr
  Register #(.width(16), .trigger("high")) register_13 (
    .D(controlled_buffer_7_out), .en(decoder_2_out12), .clk(clock_1_out), .Q(register_13_q));  // open: clr
  Register #(.width(16), .trigger("high")) register_14 (
    .D(controlled_buffer_7_out), .en(decoder_2_out13), .clk(clock_1_out), .Q(register_14_q));  // open: clr
  Register #(.width(16), .trigger("high")) register_15 (
    .D(controlled_buffer_7_out), .en(decoder_2_out14), .clk(clock_1_out), .Q(register_15_q));  // open: clr
  Register #(.width(16), .trigger("high")) ROW15 (
    .D(controlled_buffer_7_out), .en(decoder_2_out15), .clk(clock_1_out), .Q(ROW15_q));  // open: clr
  DotMatrix #(.matrixcols(16), .matrixrows(16)) dotmatrix_1 (
    .col0(ROW0_q), .col1(register_2_q), .col2(register_3_q), .col3(register_4_q), .col4(register_5_q),
    .col5(register_6_q), .col6(register_7_q), .col7(register_8_q), .col8(register_9_q), .col9(register_10_q),
    .col10(register_11_q), .col11(register_12_q), .col12(register_13_q), .col13(register_14_q),
    .col14(register_15_q), .col15(ROW15_q));

  // Notes on the sheet:
  //   so
  //   1i 1o 2i 2o 
  //   ai ar ao
  //   oi oo
  //   p1i
  //   p2i
  //   si
  //   ci co ce
  //   ii io
  //   cy
  //   contents of rom_1 (hex, n*v repeats v):
  //   286*ffff f 7 11*ffff fcff fe1f ff07 fc00 c00 10*ffff 3fbf f 1 0 0 0 9*ffff c3ff 7f 3f f 1 0 0
  //   10*ffff 87ff 1ff ff 7f 3 0 3f e1ff ffff ffff f3ff 6*ffff c7ff 1ff ff 3 3 1 f 3f ffff cfff f9ff f9ff
  //   4*ffff f3ff ff 7f 3 3 0 0 7 1f dfff f3ff 6*ffff f0ff 7f 3 3 0 0 0 7 1f e0ff f3ff 5*ffff fdff ff 7 5
  //   4*0 7 1f e1ff 5*ffff fffe 1fc 1f b 5*0 37 ff 5*ffff e7f8 1f8 1f 1 5*0 3 3f 5*ffff e0ff 7f 6*0 1 3f
  //   81ff fbff ffff ffff fffc fff0 ff 1 6*0 3 ff e3ff ffff ffff ffff ff80 ff 3 6*0 1 f 1ff fbff ffff ffff
  //   ffe0 cfe0 7f 7*0 3 3f 1ff ffff ffff ffff fff0 c0ff 3 7*0 3 3f a1f7 ffff ffff ffff e1fe 8027 3 7*0 7
  //   3d a1e3 ffff ffff ffff c0ff 1f 8*0 7 79 fbc3 ffff ffff ffff 807f 3 8*0 7 807f ffc1 ffff ffff e1ff
  //   801f 1 8*0 3 1f fdff ffff ffff e1ff 801f 10*0 7 c1c0 ff83 ffff f3ff 807f 6 10*0 80fe ff80 ffff ffff
  //   81ff f 10*0 9 e7f2 7fff ffff c1ff 1f 11*0 611f 7fff 7fff d1ff 3f 6 10*0 409f 7fff 7fff ff9f 7f 7
  //   10*0 407c 7bff 7fff ffbf f f 10*0 1c 61ff 7fff ffff 808f f 10*0 1c 60ff 7fff 7fff 406f e 10*0 3e
  //   61ff 7fff 7f8f 38 11*0 7f 73ff 7fff 7e03 18 11*0 ff 7fff 7f9f 6101 c 10*0 1e ff 3fff 3f8f 20e0 11*0
  //   1f 41ff 3fff 3f87 20b8 11*0 3f 419f 3fff 3fff 7e 11*0 3f 738f 3fff 31ff 18 11*0 3e 7f8f 3fff 20ff 8
  //   11*0 3c 3fff 3fff 20ff 18 11*0 18 7f07 3fff 61ff 19 11*0 1c 6601 3fff 73ff 3f 12*0 2101 3f8f 7fff ff
  //   12*0 2030 3f87 3fff ff 1c 11*0 38 3f8f 3fff 61bf 1f 11*0 7c 33ff 3fff 439f 3f 11*0 38 61ff 7fff 731f
  //   3f 11*0 38 20ff 3fff 7fcf 3c 11*0 3c 21ff 3fff 3fbf 38 11*0 3f 73ff 3fff 6f03 18 11*0 7f 73ff 3f9f
  //   6001 4 10*0 18 ff 7fff 3f8f 21e0 11*0 1e ff 3fff 3f87 20b8 11*0 1f 40ff 3fff 3fcf 20fe 11*0 f 40ff
  //   7fff 3fff 60cf 1f 10*0 3 c07f 7fff 7fff 7fc7 6060 7 10*0 401f 7fff 7fff 7fff 6860 30 7 10*0 7c7f
  //   7fff 7fff 7ffb 6010 f 3 9*0 4001 7fff 7fff 7fff fff0 e01c c 3 9*0 780f 7e7f 7fff 7fff fff8 2407 3
  //   5*0 1 3 1 1 1 3e3f 7f7f 7fff fffe 1f83 1 6*0 6 3 3 3 1e0f 3fff 7fff 3fff fc1 7*0 c 6 3 3 1e0f 1fff
  //   3fff 1fe3 380 7*0 18 7 7 7 1e0f 1fff 3fff 1fe7 180 7*0 18 7 7 7 1e1f 7fff 3fff 1fc7 8*0 18 f 7 6
  //   1f1e 3f7f 3fff f87 8*0 30 f 7 406 1f1e 3f7f 3fff f83 8*0 30 f 7 c06 1f1f 3f7f 3fff 781 8*0 10 f 7
  //   c07 1f1f 3f7f 3fff 781 8*0 18 f 7 c07 1f1f 3f7f 3fff 781 8*0 30 f 7 c07 1f1f 3f7f 3fff 781 8*0 30 f
  //   7 c07 1f0f 3f7f 3fff f81 8*0 30 f 7 c07 1f0f 3f7f 3fff f81 8*0 30 f 7 c07 1f0e 3f7f 3fff 1fc1 8*0 30
  //   1f 7 c07 1f0e 7fff 3fff 1fc3 8*0 20 37 f c07 3f0e 7fbf 3fff 3fe7 c0 8*0 73 f 1c07 3f0e 7fbf 3fff
  //   3fef 3c0 8*0 73 f 1c0f 3f0e ffbf 7fff 3fff 780 8*0 71 1f 1c0f 3f0e ffff 7fff 7fff f80 8*0 60 7f 1c0f
  //   3f0e ffff 7fff 7fff 1f80 8*0 60 7f 1c0e 3f0f ffff ffff 7fff 1fc0 8*0 60 7f 1c0e 3f0f 7fff ffff 7fff
  //   3fe1 8*0 40 ff 1c1e 3f0f 7fff ffff 7fff 3ff0 8*0 40 ff 1c1e 3f0f 7fff ffff 7fff 3ff0 8*0 40 ff 1c1e
  //   3f0f 7fff ffff 7fff 3ff0 8*0 40 ff 1c1e 3f0f 7fff ffff 7fff 3ff0 8*0 40 ff 1c1c 3f0f 7fff ffff 7fff
  //   3fe0 8*0 40 ff 1c1c 3f0f 7fff ffff 7fff 1fe0 8*0 60 ff 1c0c 3f8f ffff ffff 7fff 1fe0 8*0 60 7f 1c0c
  //   3f8f ffff ffff 7fff 1fc1 8*0 60 7f 1c0c 3f8f ffff 7fff 7fff 1fc1 8*0 70 7f 3c0e 3f8f ffff 7fff 7fff
  //   fc1 8*0 71 83f 3e0e bf8f ffff 7fff 3fff 7c0 8*0 73 c1f 3f07 ffaf 7fff 7fff 3fff 3c0 7*0 20 7b c0f
  //   3e07 ff8f 7fbf 7fff 3fff 40 7*0 38 3b c07 be07 ff87 7fbf 7fff 3fff 8*0 1c d 1c07 fe03 7f87 7fbf 7fff
  //   1fbf 7*0 6 6 1 de01 7e01 7f8f ffbf 7fff 1fbf 6*0 1 3 0 cc00 7e00 7f80 ff8f ffbf 3fff fbf 8*0 4000
  //   6e00 7f00 7f80 ff81 7f9f 3fff 7ff 9 8*0 3000 3f00 3f80 3fc0 7fc7 3fff 7ff f 1 9*0 3f80 1fe0 1fe0
  //   3fff 1fff 3ff 7 10*0 700 fe0 1fe0 1fff 1fff fff 3 10*0 400 1f80 1fe0 7fff 3fff 3fff 12*0 1800 3f1f
  //   3fff 3fff 8*0 1 3 7 9 18 1f 3e7f 7fff 4*0 60 1f0 ff0 ff8 3f8 180 180 80 5f 7f f7f 3fff 7*0 7c fc 7c
  //   7c fc 4 2 1 4 22*0 8000 15*0 4000 e000 15*0 3800 3800 14*0 e00 e00 14*0 380 780 300 13*0 c0 1e0 1c0
  //   13*0 60 f0 f0 13*0 30 78 70 13*0 30 7c 78 13*0 30 78 78 13*0 70 f8 78 13*0 e0 1f0 1e0 13*0 1c0 3e0
  //   1c0 13*0 380 7c0 380 13*0 780 f80 700 13*0 f80 f80 700 13*0 780 f80 780 13*0 780 7c0 780 200 12*0
  //   380 7c0 7c0 380 12*0 180 7c0 7c0 3c0 12*0 180 3e0 3e0 3c0 12*0 c0 3e0 3e0 3e0 12*0 c0 3e0 3e0 1e0
  //   12*0 1c0 3e0 3f0 1c0 12*0 1e0 3e0 3e0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
  //   contents of INS (hex, n*v repeats v):
  //   256*1008 256*406 16*1001 10001 4001 81 41 12*1 16*20 16*201 16*1001 16*11 16*1001 144*0 10400 4400
  //   480 440 12*400 16*0 30000 24000 20080 20040 12*20000 10100 4100 180 140 12*100 8800 2800 14*800 16*0
  //   16*600 240*0 10100 4100 180 140 12*100 2960*0 256*1008 256*406 16*1001 10001 4001 81 41 12*1 16*20
  //   16*201 16*1001 16*11 16*1001 144*0 10400 4400 480 440 12*400 16*0 30000 24000 20080 20040 12*20000
  //   10100 4100 180 140 12*100 8800 2800 14*800 16*0 16*600 240*0 10100 4100 180 140 12*100 2960*0
  //   256*1008 256*406 16*1001 10001 4001 81 41 12*1 16*20 16*201 16*1001 16*11 16*1001 144*0 10400 4400
  //   480 440 12*400 16*0 30000 24000 20080 20040 12*20000 10100 4100 180 140 12*100 8800 2800 14*800 16*0
  //   16*600 240*0 10100 4100 180 140 12*100 2960*0 256*1008 256*406 16*1001 10001 4001 81 41 12*1 16*20
  //   16*201 16*1001 16*11 16*1001 144*0 10400 4400 480 440 12*400 16*0 30000 24000 20080 20040 12*20000
  //   10100 4100 180 140 12*100 8800 2800 14*800 16*0 16*600 240*0 10100 4100 180 140 12*100 2960*0
  //   256*1008 256*406 16*1001 10001 4001 81 41 12*1 16*20 16*201 16*1001 16*11 16*1001 144*0 10400 4400
  //   480 440 12*400 16*0 30000 24000 20080 20040 12*20000 10100 4100 180 140 12*100 8800 2800 14*800 16*0
  //   16*600 240*0 10100 4100 180 140 12*100 2960*0 256*1008 256*406 16*1001 10001 4001 81 41 12*1 16*20
  //   16*201 16*1001 16*11 16*1001 144*0 10400 4400 480 440 12*400 16*0 30000 24000 20080 20040 12*20000
  //   10100 4100 180 140 12*100 8800 2800 14*800 16*0 16*600 240*0 10100 4100 180 140 12*100 2960*0
  //   256*1008 256*406 16*1001 10001 4001 81 41 12*1 16*20 16*201 16*1001 16*11 16*1001 144*0 10400 4400
  //   480 440 12*400 16*0 30000 24000 20080 20040 12*20000 10100 4100 180 140 12*100 8800 2800 14*800 16*0
  //   16*600 240*0 10100 4100 180 140 12*100 2960*0 256*1008 256*406 16*1001 10001 4001 81 41 12*1 16*20
  //   16*201 16*1001 16*11 16*1001 144*0 10400 4400 480 440 12*400 16*0 30000 24000 20080 20040 12*20000
  //   10100 4100 180 140 12*100 8800 2800 14*800 16*0 16*600 240*0 10100 4100 180 140 12*100 2960*0
  //   256*1008 256*406 16*1001 10001 4001 81 41 12*1 16*20 16*201 16*1001 16*11 16*1001 144*0 10400 4400
  //   480 440 12*400 16*0 30000 24000 20080 20040 12*20000 10100 4100 180 140 12*100 8800 2800 14*800 16*0
  //   16*600 240*0 10100 4100 180 140 12*100 2960*0 256*1008 256*406 16*1001 10001 4001 81 41 12*1 16*20
  //   16*201 16*1001 16*11 16*1001 144*0 10400 4400 480 440 12*400 16*0 30000 24000 20080 20040 12*20000
  //   10100 4100 180 140 12*100 8800 2800 14*800 16*0 16*600 240*0 10100 4100 180 140 12*100 2960*0
  //   256*1008 256*406 16*1001 10001 4001 81 41 12*1 16*20 16*201 16*1001 16*11 16*1001 144*0 10400 4400
  //   480 440 12*400 16*0 30000 24000 20080 20040 12*20000 10100 4100 180 140 12*100 8800 2800 14*800 16*0
  //   16*600 240*0 10100 4100 180 140 12*100 2960*0 256*1008 256*406 16*1001 10001 4001 81 41 12*1 16*20
  //   16*201 16*1001 16*11 16*1001 144*0 10400 4400 480 440 12*400 16*0 30000 24000 20080 20040 12*20000
  //   10100 4100 180 140 12*100 8800 2800 14*800 16*0 16*600 240*0 10100 4100 180 140 12*100 2960*0
  //   256*1008 256*406 16*1001 10001 4001 81 41 12*1 16*20 16*201 16*1001 16*11 16*1001 144*0 10400 4400
  //   480 440 12*400 16*0 30000 24000 20080 20040 12*20000 10100 4100 180 140 12*100 8800 2800 14*800 16*0
  //   16*600 240*0 10100 4100 180 140 12*100 2960*0 256*1008 256*406 16*1001 10001 4001 81 41 12*1 16*20
  //   16*201 16*1001 16*11 16*1001 144*0 10400 4400 480 440 12*400 16*0 30000 24000 20080 20040 12*20000
  //   10100 4100 180 140 12*100 8800 2800 14*800 16*0 16*600 240*0 10100 4100 180 140 12*100 2960*0
  //   256*1008 256*406 16*1001 10001 4001 81 41 12*1 16*20 16*201 16*1001 16*11 16*1001 144*0 10400 4400
  //   480 440 12*400 16*0 30000 24000 20080 20040 12*20000 10100 4100 180 140 12*100 8800 2800 14*800 16*0
  //   16*600 240*0 10100 4100 180 140 12*100 2960*0 256*1008 256*406 16*1001 10001 4001 81 41 12*1 16*20
  //   16*201 16*1001 16*11 16*1001 144*0 10400 4400 480 440 12*400 16*0 30000 24000 20080 20040 12*20000
  //   10100 4100 180 140 12*100 8800 2800 14*800 16*0 16*600
endmodule
